// Logisim project 2_70.circ as structural Verilog: 1 circuit, main circuit main
module main (
  input  i0,
  input  i1,
  input  i2,
  input  e,
  output d0,
  output d1,
  output d2,
  output d3,
  output d4,
  output d5,
  output d6,
  output d7
);

  and and_1 (d0, ~i0, ~i1, ~i2, e);  // AND_Gate
  and and_2 (d1, i0, ~i1, ~i2, e);  // AND_Gate
  and and_3 (d2, ~i0, i1, ~i2, e);  // AND_Gate
  and and_4 (d3, i0, i1, ~i2, e);  // AND_Gate
  and and_5 (d4, ~i0, ~i1, i2, e);  // AND_Gate
  and and_6 (d5, i0, ~i1, i2, e);  // AND_Gate
  and and_7 (d6, ~i0, i1, i2, e);  // AND_Gate
  and and_8 (d7, i0, i1, i2, e);
endmodule
