// Logisim project 2_71.circ as structural Verilog: 1 circuit, main circuit main
module main (
  input  i0,
  input  i1,
  input  i2,
  input  i3,
  input  i4,
  input  i5,
  input  i6,
  input  i7,
  input  s0,
  input  s1,
  input  s2,
  output d
);

  wire and_1_out, and_2_out, and_3_out, and_4_out, and_5_out, and_6_out, and_7_out, and_8_out;

  and and_1 (and_1_out, i0, ~s0, ~s1, ~s2);  // AND_Gate
  and and_2 (and_2_out, i1, s0, ~s1, ~s2);  // AND_Gate
  and and_3 (and_3_out, i2, ~s0, s1, ~s2);  // AND_Gate
  and and_4 (and_4_out, i3, s0, s1, ~s2);  // AND_Gate
  and and_5 (and_5_out, i4, ~s0, ~s1, s2);  // AND_Gate
  and and_6 (and_6_out, i5, s0, ~s1, s2);  // AND_Gate
  and and_7 (and_7_out, i6, ~s0, s1, s2);  // AND_Gate
  and and_8 (and_8_out, i7, s0, s1, s2);
  or or_1 (d, and_1_out, and_2_out, and_3_out, and_4_out, and_5_out, and_6_out, and_7_out, and_8_out);
endmodule
