// Logisim project 3_40.circ as structural Verilog: 1 circuit, main circuit main
module main (
  input  a,
  input  b,
  output y
);

  wire and_1_out, and_2_out, and_3_out, and_4_out, and_5_out, clock_1_out, d_ff_1_q, d_ff_2_q, or_1_out,
       or_2_out, or_3_out, or_4_out;

  D_Flip_Flop d_ff_1 (.D(or_3_out), .clk(clock_1_out), .Q(d_ff_1_q));  // open: Qn, preset, reset
  Clock clock_1 (.out(clock_1_out));
  D_Flip_Flop d_ff_2 (.D(or_4_out), .clk(clock_1_out), .Q(d_ff_2_q));  // open: Qn, preset, reset
  and and_1 (and_1_out, ~a, ~b, ~d_ff_2_q);  // AND_Gate
  or or_1 (or_1_out, and_1_out, d_ff_2_q);
  and and_2 (and_2_out, or_1_out, ~d_ff_1_q);  // AND_Gate
  xor xor_1 (y, d_ff_1_q, d_ff_2_q);
  and and_3 (and_3_out, b, d_ff_1_q, ~d_ff_2_q);  // AND_Gate
  or or_2 (or_2_out, d_ff_2_q, b);
  or or_3 (or_3_out, and_3_out, and_2_out);
  and and_4 (and_4_out, ~a, or_2_out, ~d_ff_1_q);  // AND_Gate
  and and_5 (and_5_out, d_ff_1_q, ~d_ff_2_q);  // AND_Gate
  or or_4 (or_4_out, and_5_out, and_4_out);

  // Notes on the sheet:
  //   1
  //   0
endmodule
