// Logisim project 3_43.circ as structural Verilog: 1 circuit, main circuit main
module main (
  input  gcnt,
  output x,
  output y,
  output z
);

  wire and_1_out, and_2_out, and_3_out, and_4_out, and_5_out, and_6_out, clock_1_out, d_ff_1_q, d_ff_2_q,
       d_ff_3_qn, nand_1_out, not_1_out, or_1_out, or_2_out, or_3_out, xor_1_out, xor_2_out;

  and and_1 (and_1_out, x, not_1_out);
  or or_1 (or_1_out, and_1_out, and_2_out);
  and and_2 (and_2_out, gcnt, or_2_out);
  or or_2 (or_2_out, and_3_out, and_4_out);
  or or_3 (or_3_out, and_5_out, and_6_out);
  and and_3 (and_3_out, d_ff_1_q, d_ff_2_q, d_ff_3_qn);
  and and_4 (and_4_out, x, nand_1_out);
  and and_5 (and_5_out, not_1_out, d_ff_2_q);
  and and_6 (and_6_out, gcnt, xor_1_out);
  nand nand_1 (nand_1_out, d_ff_2_q, d_ff_1_q);
  xor xor_1 (xor_1_out, d_ff_2_q, d_ff_1_q);
  xor xor_2 (xor_2_out, gcnt, d_ff_1_q);
  D_Flip_Flop d_ff_1 (.D(xor_2_out), .clk(clock_1_out), .Q(d_ff_1_q));  // open: Qn, preset, reset
  D_Flip_Flop d_ff_2 (.D(or_3_out), .clk(clock_1_out), .Q(d_ff_2_q));  // open: Qn, preset, reset
  D_Flip_Flop d_ff_3 (.D(or_1_out), .clk(clock_1_out), .Q(x), .Qn(d_ff_3_qn));  // open: preset, reset
  Clock clock_1 (.out(clock_1_out));
  not not_1 (not_1_out, gcnt);
  xor xor_3 (y, d_ff_1_q, d_ff_2_q);
  xor xor_4 (z, d_ff_2_q, x);

  // Notes on the sheet:
  //   0
  //   1
  //   2
endmodule
