// Logisim project 4.13.circ as structural Verilog: 1 circuit, main circuit main
module main (
  input  [7:0] in_1,
  input  [7:0] in_2,
  input  [7:0] in_3,
  input  [7:0] in_4,
  output [7:0] out_5
);

  wire adder_1_cout, adder_2_cout;
  wire [7:0] adder_1_out, adder_2_out;

  Adder adder_1 (.a(in_1), .b(in_2), .out(adder_1_out), .cout(adder_1_cout));  // open: cin
  Adder adder_2 (.a(adder_1_out), .b(in_3), .out(adder_2_out), .cin(adder_1_cout), .cout(adder_2_cout));
  Adder adder_3 (.a(adder_2_out), .b(in_4), .out(out_5), .cin(adder_2_cout));  // open: cout
endmodule
