// Logisim project 4.21.circ as structural Verilog: 1 circuit, main circuit main
module main (
  input  [15:0] in_1,
  input  [15:0] in_2,
  output [15:0] out_3
);

  wire comparator_1_eq, comparator_1_gt, comparator_1_lt;

  assign out_3 = comparator_1_gt ? in_1 : 16'bz;  // Controlled_Buffer controlled_buffer_1
  Comparator #(.width(16)) comparator_1 (
    .a(in_1), .b(in_2), .gt(comparator_1_gt), .eq(comparator_1_eq), .lt(comparator_1_lt));
  assign out_3 = comparator_1_eq ? in_1 : 16'bz;  // Controlled_Buffer controlled_buffer_2
  assign out_3 = comparator_1_lt ? in_2 : 16'bz;  // Controlled_Buffer controlled_buffer_3
endmodule
