// Logisim project 4.40.circ as structural Verilog: 1 circuit, main circuit main
module main (
  input  x,
  input  [7:0] A,
  input  y,
  input  z,
  input  [7:0] B,
  output [7:0] S
);

  wire and_1_out;
  wire [7:0] multiplexer_1_out, multiplexer_2_out, nand_1_out, not_1_out, not_2_out, shifter_2_out, xor_1_out;

  Shifter shifter_1 (.in(A), .\dist (3'b111), .out(A));
  Shifter #(.shift("lr")) shifter_2 (.in(A), .\dist (3'b111), .out(shifter_2_out));
  assign xor_1_out = A ^ B;  // XOR_Gate xor_1, 8 bits wide
  assign not_1_out = ~A;  // NOT_Gate not_1, 8 bits wide
  assign nand_1_out = ~(A & B);  // NAND_Gate nand_1, 8 bits wide
  assign not_2_out = ~B;  // NOT_Gate not_2, 8 bits wide
  Multiplexer #(.select(3), .width(8)) multiplexer_1 (
    .in0(A), .in1(A), .in2(A), .in3(shifter_2_out), .in4(nand_1_out), .in5(xor_1_out),
    .in6({A[0], A[1], A[2], A[3], A[4], A[5], A[6], A[7]}), .in7(not_1_out), .out(multiplexer_1_out),
    .sel({x, y, z}));
  and and_1 (and_1_out, ~z, ~y, ~x);  // AND_Gate
  Multiplexer #(.select(3), .width(8)) multiplexer_2 (
    .in0(not_2_out), .in1(B), .in2({8{1'b0}}), .in3({8{1'b0}}), .in4({8{1'b0}}), .in5({8{1'b0}}),
    .in6({8{1'b0}}), .in7({8{1'b0}}), .out(multiplexer_2_out), .sel({x, y, z}));
  Adder adder_1 (.a(multiplexer_1_out), .b(multiplexer_2_out), .out(S), .cin(and_1_out));  // open: cout
endmodule
