// Logisim project 4.62.circ as structural Verilog: 1 circuit, main circuit main
module main (
  input  [3:0] W_data,
  input  [1:0] R1_addr,
  input  [1:0] W_addr,
  input  R1_en,
  input  W_en,
  input  [1:0] R2_addr,
  input  R2_en,
  output [3:0] R1_data,
  output [3:0] R2_data
);

  wire clock_1_out, decoder_1_out0, decoder_1_out1, decoder_1_out2, decoder_1_out3, decoder_2_out0,
       decoder_2_out1, decoder_2_out2, decoder_2_out3, decoder_3_out0, decoder_3_out1, decoder_3_out2,
       decoder_3_out3;
  wire [3:0] register_1_q, register_2_q, register_3_q, register_4_q;

  Register #(.width(4)) register_1 (.D(W_data), .en(decoder_1_out0), .clk(clock_1_out), .Q(register_1_q));  // open: clr
  Register #(.width(4)) register_2 (.D(W_data), .en(decoder_1_out1), .clk(clock_1_out), .Q(register_2_q));  // open: clr
  Decoder #(.select(2)) decoder_1 (
    .out0(decoder_1_out0), .out1(decoder_1_out1), .out2(decoder_1_out2), .out3(decoder_1_out3), .sel(W_addr),
    .en(W_en));
  Register #(.width(4)) register_3 (.D(W_data), .en(decoder_1_out2), .clk(clock_1_out), .Q(register_3_q));  // open: clr
  Register #(.width(4)) register_4 (.D(W_data), .en(decoder_1_out3), .clk(clock_1_out), .Q(register_4_q));  // open: clr
  Clock clock_1 (.out(clock_1_out));
  assign R1_data = decoder_2_out0 ? register_1_q : 4'bz;  // Controlled_Buffer controlled_buffer_1
  assign R2_data = decoder_3_out0 ? register_1_q : 4'bz;  // Controlled_Buffer controlled_buffer_2
  Decoder #(.select(2)) decoder_2 (
    .out0(decoder_2_out0), .out1(decoder_2_out1), .out2(decoder_2_out2), .out3(decoder_2_out3),
    .sel(R1_addr), .en(R1_en));
  assign R1_data = decoder_2_out1 ? register_2_q : 4'bz;  // Controlled_Buffer controlled_buffer_3
  assign R2_data = decoder_3_out1 ? register_2_q : 4'bz;  // Controlled_Buffer controlled_buffer_4
  assign R1_data = decoder_2_out2 ? register_3_q : 4'bz;  // Controlled_Buffer controlled_buffer_5
  assign R2_data = decoder_3_out2 ? register_3_q : 4'bz;  // Controlled_Buffer controlled_buffer_6
  assign R1_data = decoder_2_out3 ? register_4_q : 4'bz;  // Controlled_Buffer controlled_buffer_7
  assign R2_data = decoder_3_out3 ? register_4_q : 4'bz;  // Controlled_Buffer controlled_buffer_8
  Decoder #(.select(2)) decoder_3 (
    .out0(decoder_3_out0), .out1(decoder_3_out1), .out2(decoder_3_out2), .out3(decoder_3_out3),
    .sel(R2_addr), .en(R2_en));
endmodule
