// Logisim project circuit.circ as structural Verilog: 1 circuit, main circuit main
module main (
  input  a,
  input  b,
  input  c,
  output F,
  output F_IC,
  output G,
  output G_IC
);

  wire and_1_out, and_2_out, and_3_out, and_4_out, and_5_out, and_6_out, and_7_out, n7408_1_pin3,
       n7408_1_pin6, n7408_1_pin11, n7411_1_pin8, n7432_1_pin3, n7432_1_pin6, not_1_out, not_2_out,
       not_3_out, not_4_out, not_5_out, not_6_out;

  and and_1 (and_1_out, a, b, c);
  and and_2 (and_2_out, a, b);
  and and_3 (and_3_out, b, c);
  and and_4 (and_4_out, c, a);
  not not_1 (not_1_out, a);
  and and_5 (and_5_out, not_1_out, not_2_out);
  not not_2 (not_2_out, b);
  not not_3 (not_3_out, a);
  and and_6 (and_6_out, not_3_out, b, not_4_out);
  not not_4 (not_4_out, c);
  not not_5 (not_5_out, b);
  and and_7 (and_7_out, a, not_5_out, not_6_out);
  not not_6 (not_6_out, c);
  or or_1 (F, and_1_out, and_2_out, and_3_out, and_4_out);
  or or_2 (G, and_5_out, and_6_out, and_7_out);
  _7411 #(.ShowInternalStructure("true")) u_7411_1 (
    .pin11(a), .pin10(b), .pin9(c), .pin8(n7411_1_pin8));  // open: pin1, pin2, pin3, pin4, pin5, pin6, pin13, pin12
  _7408 #(.ShowInternalStructure("true")) u_7408_1 (
    .pin1(a), .pin2(b), .pin3(n7408_1_pin3), .pin4(b), .pin5(c), .pin6(n7408_1_pin6), .pin13(c), .pin12(a),
    .pin11(n7408_1_pin11));  // open: pin10, pin9, pin8
  _7432 #(.ShowInternalStructure("true")) u_7432_1 (
    .pin1(n7408_1_pin11), .pin2(n7408_1_pin6), .pin3(n7432_1_pin3), .pin4(n7432_1_pin3), .pin5(n7408_1_pin3),
    .pin6(n7432_1_pin6), .pin10(n7411_1_pin8), .pin9(n7432_1_pin6), .pin8(F_IC));  // open: pin13, pin12, pin11
endmodule
