// Logisim project part1.circ as structural Verilog: 1 circuit, main circuit main
module main (
  input  a,
  input  b,
  input  c,
  output F,
  output F_IC,
  output G,
  output G_IC
);

  wire and_1_out, and_2_out, and_3_out, and_4_out, and_5_out, and_6_out, and_7_out, n7404_1_pin2,
       n7404_1_pin4, n7404_1_pin6, n7408_1_pin3, n7408_1_pin6, n7408_1_pin11, n7408_2_pin8, n7411_1_pin8,
       n7411_2_pin8, n7411_2_pin12, n7432_1_pin3, n7432_1_pin6, n7432_2_pin3;

  and and_1 (and_1_out, a, b, c);
  and and_2 (and_2_out, a, b);
  and and_3 (and_3_out, b, c);
  and and_4 (and_4_out, c, a);
  and and_5 (and_5_out, ~a, ~b);  // AND_Gate
  and and_6 (and_6_out, ~a, b, ~c);  // AND_Gate
  and and_7 (and_7_out, a, ~b, ~c);  // AND_Gate
  or or_1 (F, and_1_out, and_2_out, and_3_out, and_4_out);
  or or_2 (G, and_5_out, and_6_out, and_7_out);
  _7404 #(.ShowInternalStructure("true")) u_7404_1 (
    .pin1(a), .pin2(n7404_1_pin2), .pin3(b), .pin4(n7404_1_pin4), .pin5(c), .pin6(n7404_1_pin6));  // open: pin13, pin12, pin11, pin10, pin9, pin8
  _7411 #(.ShowInternalStructure("true")) u_7411_1 (
    .pin11(a), .pin10(b), .pin9(c), .pin8(n7411_1_pin8));  // open: pin1, pin2, pin3, pin4, pin5, pin6, pin13, pin12
  _7411 #(.ShowInternalStructure("true")) u_7411_2 (
    .pin1(n7404_1_pin2), .pin2(b), .pin13(n7404_1_pin6), .pin12(n7411_2_pin12), .pin11(n7404_1_pin6),
    .pin10(n7404_1_pin4), .pin9(a), .pin8(n7411_2_pin8));  // open: pin3, pin4, pin5, pin6
  _7408 #(.ShowInternalStructure("true")) u_7408_1 (
    .pin1(a), .pin2(b), .pin3(n7408_1_pin3), .pin4(b), .pin5(c), .pin6(n7408_1_pin6), .pin13(c), .pin12(a),
    .pin11(n7408_1_pin11));  // open: pin10, pin9, pin8
  _7408 #(.ShowInternalStructure("true")) u_7408_2 (
    .pin10(n7404_1_pin4), .pin9(n7404_1_pin2), .pin8(n7408_2_pin8));  // open: pin1, pin2, pin3, pin4, pin5, pin6, pin13, pin12, pin11
  _7432 #(.ShowInternalStructure("true")) u_7432_1 (
    .pin1(n7408_1_pin11), .pin2(n7408_1_pin6), .pin3(n7432_1_pin3), .pin4(n7432_1_pin3), .pin5(n7408_1_pin3),
    .pin6(n7432_1_pin6), .pin10(n7411_1_pin8), .pin9(n7432_1_pin6), .pin8(F_IC));  // open: pin13, pin12, pin11
  _7432 #(.ShowInternalStructure("true")) u_7432_2 (
    .pin1(n7411_2_pin12), .pin2(n7411_2_pin8), .pin3(n7432_2_pin3), .pin4(n7432_2_pin3), .pin5(n7408_2_pin8),
    .pin6(G_IC));  // open: pin13, pin12, pin11, pin10, pin9, pin8
endmodule
