// Logisim project part2.circ as structural Verilog: 3 circuits, main circuit encoder
module main (
  input  Car_0,
  input  Car_1,
  input  Car_2,
  input  Car_3,
  input  Car_4,
  input  Car_5,
  input  Car_6,
  input  Car_7,
  input  Car_8,
  input  Car_9
);

  wire dec0der_1_o0, dec0der_1_o1, dec0der_1_o2, dec0der_1_o3, dec0der_1_o4, dec0der_1_o5, dec0der_1_o6,
       encoder_1_o0, encoder_1_o1, encoder_1_o2, encoder_1_o3;

  encoder encoder_1 (
    .i0(Car_0), .i1(Car_1), .i2(Car_2), .i3(Car_3), .i4(Car_4), .i5(Car_5), .i6(Car_6), .i7(Car_7),
    .i8(Car_8), .i9(Car_9), .o0(encoder_1_o0), .o1(encoder_1_o1), .o2(encoder_1_o2), .o3(encoder_1_o3));
  dec0der dec0der_1 (
    .i0(encoder_1_o0), .i1(encoder_1_o1), .i2(encoder_1_o2), .i3(encoder_1_o3), .o0(dec0der_1_o0),
    .o1(dec0der_1_o1), .o2(dec0der_1_o2), .o3(dec0der_1_o3), .o4(dec0der_1_o4), .o5(dec0der_1_o5),
    .o6(dec0der_1_o6));
  _7_Segment_Display #(.decimalPoint("false")) u_7_segment_display_1 (
    .g(dec0der_1_o0), .f(dec0der_1_o1), .a(dec0der_1_o2), .b(dec0der_1_o3), .e(dec0der_1_o4),
    .d(dec0der_1_o5), .c(dec0der_1_o6));
endmodule

module encoder (
  input  i0,
  input  i1,
  input  i2,
  input  i3,
  input  i4,
  input  i5,
  input  i6,
  input  i7,
  input  i8,
  input  i9,
  output o0,
  output o1,
  output o2,
  output o3
);

  wire n7432_1_pin3, n7432_1_pin6, n7432_1_pin11, n7432_2_pin3, n7432_2_pin6, n7432_2_pin11, n7432_3_pin3,
       n7432_3_pin11, n7432_4_pin3;

  _7432 #(.ShowInternalStructure("true")) u_7432_1 (
    .pin1(i4), .pin2(i2), .pin3(n7432_1_pin3), .pin4(n7432_1_pin3), .pin5(i0), .pin6(n7432_1_pin6),
    .pin13(i6), .pin12(i8), .pin11(n7432_1_pin11), .pin10(n7432_1_pin11), .pin9(n7432_1_pin6), .pin8(o0));
  _7432 #(.ShowInternalStructure("true")) u_7432_2 (
    .pin1(i5), .pin2(i2), .pin3(n7432_2_pin3), .pin4(n7432_2_pin3), .pin5(i1), .pin6(n7432_2_pin6),
    .pin13(i6), .pin12(i9), .pin11(n7432_2_pin11), .pin10(n7432_2_pin11), .pin9(n7432_2_pin6), .pin8(o1));
  _7432 #(.ShowInternalStructure("true")) u_7432_3 (
    .pin1(i4), .pin2(i3), .pin3(n7432_3_pin3), .pin13(i5), .pin12(i6), .pin11(n7432_3_pin11),
    .pin10(n7432_3_pin11), .pin9(n7432_3_pin3), .pin8(o2));  // open: pin4, pin5, pin6
  _7432 #(.ShowInternalStructure("true")) u_7432_4 (
    .pin1(i7), .pin2(i8), .pin3(n7432_4_pin3), .pin4(n7432_4_pin3), .pin5(i9), .pin6(o3));  // open: pin13, pin12, pin11, pin10, pin9, pin8
endmodule

module dec0der (
  input  i0,
  input  i1,
  input  i2,
  input  i3,
  output o0,
  output o1,
  output o2,
  output o3,
  output o4,
  output o5,
  output o6
);

  wire n7404_1_pin2, n7404_1_pin4, n7404_1_pin6, n7404_1_pin12, n7408_1_pin3, n7408_1_pin6, n7408_1_pin8,
       n7408_1_pin11, n7408_2_pin4, n7408_2_pin11, n7408_3_pin5, n7408_3_pin10, n7408_3_pin11, n7421_1_pin8,
       n7421_2_pin6, n7421_2_pin8, n7421_3_pin6, n7421_3_pin8, n7432_1_pin3, n7432_1_pin6, n7432_3_pin3,
       n7432_4_pin3;

  _7404 #(.ShowInternalStructure("true")) u_7404_1 (
    .pin1(i3), .pin2(n7404_1_pin2), .pin3(i2), .pin4(n7404_1_pin4), .pin5(i1), .pin6(n7404_1_pin6),
    .pin13(i0), .pin12(n7404_1_pin12));  // open: pin11, pin10, pin9, pin8
  _7421 #(.ShowInternalStructure("true")) u_7421_1 (
    .pin13(n7404_1_pin2), .pin12(n7404_1_pin4), .pin10(i1), .pin9(i0), .pin8(n7421_1_pin8));  // open: pin1, pin2, pin3, pin4, pin5, pin6, pin11
  _7404 #(.ShowInternalStructure("true")) u_7404_2 (
    .pin5(n7421_1_pin8), .pin6(o6));  // open: pin1, pin2, pin3, pin4, pin13, pin12, pin11, pin10, pin9, pin8
  _7408 #(.ShowInternalStructure("true")) u_7408_1 (
    .pin1(n7404_1_pin4), .pin2(n7404_1_pin6), .pin3(n7408_1_pin3), .pin4(i2), .pin5(i1), .pin6(n7408_1_pin6),
    .pin13(n7404_1_pin4), .pin12(i1), .pin11(n7408_1_pin11), .pin10(n7408_1_pin11), .pin9(i0),
    .pin8(n7408_1_pin8));
  _7432 #(.ShowInternalStructure("true")) u_7432_1 (
    .pin1(n7408_1_pin6), .pin2(n7408_1_pin3), .pin3(n7432_1_pin3), .pin4(n7432_1_pin3), .pin5(n7408_1_pin8),
    .pin6(n7432_1_pin6));  // open: pin13, pin12, pin11, pin10, pin9, pin8
  _7408 #(.ShowInternalStructure("true")) u_7408_2 (
    .pin1(n7432_1_pin6), .pin2(n7404_1_pin2), .pin4(n7408_2_pin4), .pin5(i0), .pin6(o5), .pin13(i3),
    .pin12(n7404_1_pin4), .pin11(n7408_2_pin11), .pin10(n7408_2_pin11), .pin9(n7404_1_pin6),
    .pin8(n7408_2_pin4));  // open: pin3
  _7408 #(.ShowInternalStructure("true")) u_7408_3 (
    .pin4(i0), .pin5(n7408_3_pin5), .pin6(o4), .pin13(i3), .pin12(n7404_1_pin6), .pin11(n7408_3_pin11),
    .pin10(n7408_3_pin10), .pin9(n7404_1_pin4), .pin8(n7408_3_pin5));  // open: pin1, pin2, pin3
  _7432 #(.ShowInternalStructure("true")) u_7432_2 (
    .pin1(n7408_3_pin11), .pin2(n7404_1_pin2), .pin3(n7408_3_pin10));  // open: pin4, pin5, pin6, pin13, pin12, pin11, pin10, pin9, pin8
  _7421 #(.ShowInternalStructure("true")) u_7421_2 (
    .pin1(n7404_1_pin12), .pin2(i1), .pin4(i2), .pin5(n7404_1_pin2), .pin6(n7421_2_pin6),
    .pin13(n7404_1_pin2), .pin12(i2), .pin10(i1), .pin9(i0), .pin8(n7421_2_pin8));  // open: pin3, pin11
  _7432 #(.ShowInternalStructure("true")) u_7432_3 (
    .pin1(n7421_2_pin8), .pin2(n7421_2_pin6), .pin3(n7432_3_pin3));  // open: pin4, pin5, pin6, pin13, pin12, pin11, pin10, pin9, pin8
  _7404 #(.ShowInternalStructure("true")) u_7404_3 (
    .pin1(n7432_3_pin3), .pin2(o3));  // open: pin3, pin4, pin5, pin6, pin13, pin12, pin11, pin10, pin9, pin8
  _7421 #(.ShowInternalStructure("true")) u_7421_3 (
    .pin1(i0), .pin2(i1), .pin4(n7404_1_pin4), .pin5(n7404_1_pin2), .pin6(n7421_3_pin6),
    .pin13(n7404_1_pin2), .pin12(i2), .pin10(n7404_1_pin6), .pin9(n7404_1_pin12), .pin8(n7421_3_pin8));  // open: pin3, pin11
  _7432 #(.ShowInternalStructure("true")) u_7432_4 (
    .pin1(n7421_3_pin8), .pin2(n7421_3_pin6), .pin3(n7432_4_pin3));  // open: pin4, pin5, pin6, pin13, pin12, pin11, pin10, pin9, pin8
  _7404 #(.ShowInternalStructure("true")) u_7404_4 (
    .pin1(n7432_4_pin3), .pin2(o2));  // open: pin3, pin4, pin5, pin6, pin13, pin12, pin11, pin10, pin9, pin8
endmodule
