// Logisim project part2.circ as structural Verilog: 1 circuit, main circuit main
module main (
  input  Car_0,
  input  Car_1,
  input  Car_2,
  input  Car_3,
  input  Car_4,
  input  Car_5,
  input  Car_6,
  input  Car_7,
  input  Car_8,
  input  Car_9
);

  _7_Segment_Display u_7_segment_display_1 ();  // open: g, f, a, b, e, d, c, dp
endmodule
