// Logisim project problem1.circ as structural Verilog: 5 circuits, main circuit main
module main (
  input  in_1,
  input  in_2,
  output out_3
);

  wire dlatch_1_out_4, not_with_nand_1_out_2;

  not_with_nand not_with_nand_1 (.in_1(in_2), .out_2(not_with_nand_1_out_2));
  dlatch dlatch_1 (.in_1(in_1), .in_2(not_with_nand_1_out_2), .out_4(dlatch_1_out_4));  // open: out_3
  dlatch dlatch_2 (.in_1(dlatch_1_out_4), .in_2(in_2), .out_4(out_3));  // open: out_3
endmodule

module not_with_nand (
  input  in_1,
  output out_2
);

  nand nand_1 (out_2, in_1, in_1);
endmodule

module and_with_nand (
  input  in_1,
  input  in_2,
  output out_3
);

  wire nand_1_out;

  nand nand_1 (nand_1_out, in_1, in_2);
  nand nand_2 (out_3, nand_1_out, nand_1_out);
endmodule

module nor_with_nand (
  input  in_1,
  input  in_2,
  output out_3
);

  wire nand_1_out, nand_2_out, nand_3_out;

  nand nand_1 (nand_1_out, in_1, in_1);
  nand nand_2 (nand_2_out, in_2, in_2);
  nand nand_3 (nand_3_out, nand_1_out, nand_2_out);
  nand nand_4 (out_3, nand_3_out, nand_3_out);
endmodule

module dlatch (
  input  in_1,
  input  in_2,
  output out_3,
  output out_4
);

  wire and_with_nand_1_out_3, and_with_nand_2_out_3, not_with_nand_1_out_2;

  not_with_nand not_with_nand_1 (.in_1(in_1), .out_2(not_with_nand_1_out_2));
  and_with_nand and_with_nand_1 (.in_1(in_1), .in_2(in_2), .out_3(and_with_nand_1_out_3));
  and_with_nand and_with_nand_2 (.in_1(in_2), .in_2(not_with_nand_1_out_2), .out_3(and_with_nand_2_out_3));
  nor_with_nand nor_with_nand_1 (.in_1(and_with_nand_1_out_3), .in_2(out_4), .out_3(out_3));
  nor_with_nand nor_with_nand_2 (.in_1(out_3), .in_2(and_with_nand_2_out_3), .out_3(out_4));
endmodule
