// Logisim project problem2.circ as structural Verilog: 1 circuit, main circuit main
module main (
);

  wire and_1_out, and_2_out, button_1_out, clock_1_out, d_ff_1_q, d_ff_2_q, not_1_out, or_1_out, xor_1_out,
       xor_2_out;

  Button button_1 (.out(button_1_out));
  Clock clock_1 (.out(clock_1_out));
  D_Flip_Flop d_ff_1 (.D(button_1_out), .clk(clock_1_out), .Q(d_ff_1_q));  // open: Qn, preset, reset
  D_Flip_Flop d_ff_2 (.D(or_1_out), .clk(clock_1_out), .Q(d_ff_2_q));  // open: Qn, preset, reset
  not not_1 (not_1_out, button_1_out);
  xor xor_1 (xor_1_out, d_ff_2_q, d_ff_1_q);
  xor xor_2 (xor_2_out, d_ff_1_q, d_ff_2_q);
  LED led_1 (.in(xor_2_out));
  and and_1 (and_1_out, d_ff_2_q, button_1_out);
  and and_2 (and_2_out, not_1_out, xor_1_out);
  or or_1 (or_1_out, and_1_out, and_2_out);

  // Notes on the sheet:
  //   0
  //   1
  //   7486
  //   7486
  //   7408
  //   7404
  //   7408
  //   7432
endmodule
