// Logisim project problem3.circ as structural Verilog: 2 circuits, main circuit main
module main (
  input  IO_enable,
  input  [3:0] address_bus,
  output headlights,
  output door_1_lock,
  output door_2_lock,
  output door_3_lock,
  output door_4_lock,
  output left_indicator,
  output right_indicator,
  output wipers
);

  wire clk_out, decoder_1_out0, decoder_1_out1, decoder_1_out2, decoder_1_out3, decoder_1_out4,
       decoder_1_out5, decoder_1_out6, decoder_1_out7;

  Clock clk (.out(clk_out));
  Decoder #(.select(3)) decoder_1 (
    .out0(decoder_1_out0), .out1(decoder_1_out1), .out2(decoder_1_out2), .out3(decoder_1_out3),
    .out4(decoder_1_out4), .out5(decoder_1_out5), .out6(decoder_1_out6), .out7(decoder_1_out7),
    .sel(address_bus[2:0]), .en(IO_enable));
  \logic  logic_1 (.Bs(decoder_1_out0), .b3(address_bus[3]), .Clk(clk_out), .a(headlights));
  \logic  logic_2 (.Bs(decoder_1_out1), .b3(address_bus[3]), .Clk(clk_out), .a(door_1_lock));
  \logic  logic_3 (.Bs(decoder_1_out2), .b3(address_bus[3]), .Clk(clk_out), .a(door_2_lock));
  \logic  logic_4 (.Bs(decoder_1_out3), .b3(address_bus[3]), .Clk(clk_out), .a(door_3_lock));
  \logic  logic_5 (.Bs(decoder_1_out4), .b3(address_bus[3]), .Clk(clk_out), .a(door_4_lock));
  \logic  logic_6 (.Bs(decoder_1_out5), .b3(address_bus[3]), .Clk(clk_out), .a(left_indicator));
  \logic  logic_7 (.Bs(decoder_1_out6), .b3(address_bus[3]), .Clk(clk_out), .a(right_indicator));
  \logic  logic_8 (.Bs(decoder_1_out7), .b3(address_bus[3]), .Clk(clk_out), .a(wipers));
endmodule

module \logic  (
  input  Bs,
  input  b3,
  input  Clk,
  output a
);

  wire and_1_out, and_2_out, or_1_out, xor_1_out, xor_2_out;

  xor xor_1 (xor_1_out, b3, Bs);
  xor xor_2 (xor_2_out, Bs, a);
  and and_1 (and_1_out, xor_2_out, b3);
  and and_2 (and_2_out, ~xor_1_out, a);  // AND_Gate
  or or_1 (or_1_out, and_2_out, and_1_out);
  D_Flip_Flop d_ff_1 (.D(or_1_out), .clk(Clk), .Q(a));  // open: Qn, preset, reset
endmodule
