// Logisim project problem3simpler.circ as structural Verilog: 1 circuit, main circuit main
module main (
);

  wire button_1_out, clock_1_out, d_ff_1_q, xor_1_out;

  xor xor_1 (xor_1_out, button_1_out, d_ff_1_q);
  Clock clock_1 (.out(clock_1_out));
  LED led_1 (.in(d_ff_1_q));
  D_Flip_Flop d_ff_1 (.D(xor_1_out), .clk(clock_1_out), .Q(d_ff_1_q));  // open: Qn, preset, reset
  Button button_1 (.out(button_1_out));
endmodule
