// Logisim project Lab4.circ as structural Verilog: 13 circuits, main circuit FullAdder
module FullAdder (
  input  a,
  input  b,
  input  ci,
  output s,
  output co
);

  wire and_1_out, and_2_out, and_3_out;

  ExactlyOne xor_1 (.out(s), .in0(a), .in1(b), .in2(ci));
  and and_1 (and_1_out, a, b);
  and and_2 (and_2_out, a, ci);
  and and_3 (and_3_out, b, ci);
  or or_1 (co, and_1_out, and_2_out, and_3_out);
endmodule

module EightBitAdder (
  input  Ci,
  input  [7:0] A,
  input  [7:0] B,
  output Co,
  output [7:0] sum
);

  wire fulladder_1_co, fulladder_2_co, fulladder_3_co, fulladder_4_co, fulladder_5_co, fulladder_6_co,
       fulladder_7_co;

  FullAdder fulladder_1 (.a(A[0]), .b(B[0]), .ci(Ci), .s(sum[0]), .co(fulladder_1_co));
  FullAdder fulladder_2 (.a(A[1]), .b(B[1]), .ci(fulladder_1_co), .s(sum[1]), .co(fulladder_2_co));
  FullAdder fulladder_3 (.a(A[2]), .b(B[2]), .ci(fulladder_2_co), .s(sum[2]), .co(fulladder_3_co));
  FullAdder fulladder_4 (.a(A[3]), .b(B[3]), .ci(fulladder_3_co), .s(sum[3]), .co(fulladder_4_co));
  FullAdder fulladder_5 (.a(A[4]), .b(B[4]), .ci(fulladder_4_co), .s(sum[4]), .co(fulladder_5_co));
  FullAdder fulladder_6 (.a(A[5]), .b(B[5]), .ci(fulladder_5_co), .s(sum[5]), .co(fulladder_6_co));
  FullAdder fulladder_7 (.a(A[6]), .b(B[6]), .ci(fulladder_6_co), .s(sum[6]), .co(fulladder_7_co));
  FullAdder fulladder_8 (.a(A[7]), .b(B[7]), .ci(fulladder_7_co), .s(sum[7]), .co(Co));
endmodule

module EightBitSubtractor (
  input  [7:0] A,
  input  [7:0] B,
  output [7:0] Difference
);

  wire [7:0] not_1_out;

  assign not_1_out = ~B;  // NOT_Gate not_1, 8 bits wide
  EightBitAdder eightbitadder_1 (.Ci(1'b1), .A(A), .B(not_1_out), .sum(Difference));  // open: Co
endmodule

module MagnitudeComparator (
  input  A,
  input  B,
  input  Igt,
  input  Ieq,
  input  Ilt,
  output AgtB,
  output AeqB,
  output AltB
);

  wire and_1_out, and_2_out, and_3_out, and_5_out, not_1_out, not_2_out, not_3_out, not_4_out, not_5_out,
       xor_1_out;

  not not_1 (not_1_out, B);
  not not_2 (not_2_out, A);
  and and_1 (and_1_out, A, not_1_out);
  not not_3 (not_3_out, Ilt);
  xor xor_1 (xor_1_out, B, A);
  not not_4 (not_4_out, xor_1_out);
  not not_5 (not_5_out, Igt);
  and and_2 (and_2_out, not_2_out, B);
  and and_3 (and_3_out, and_1_out, not_3_out);
  and and_4 (AeqB, not_4_out, Ieq);
  and and_5 (and_5_out, not_5_out, and_2_out);
  or or_1 (AgtB, and_3_out, Igt);
  or or_2 (AltB, Ilt, and_5_out);
endmodule

module EightBitComp (
  input  [7:0] A,
  input  [7:0] B,
  output AgtB,
  output AeqB,
  output AltB
);

  wire magnitudecomparator_1_aeqb, magnitudecomparator_1_agtb, magnitudecomparator_1_altb,
       magnitudecomparator_2_aeqb, magnitudecomparator_2_agtb, magnitudecomparator_2_altb,
       magnitudecomparator_3_aeqb, magnitudecomparator_3_agtb, magnitudecomparator_3_altb,
       magnitudecomparator_4_aeqb, magnitudecomparator_4_agtb, magnitudecomparator_4_altb,
       magnitudecomparator_5_aeqb, magnitudecomparator_5_agtb, magnitudecomparator_5_altb,
       magnitudecomparator_6_aeqb, magnitudecomparator_6_agtb, magnitudecomparator_6_altb,
       magnitudecomparator_7_aeqb, magnitudecomparator_7_agtb, magnitudecomparator_7_altb, not_1_out,
       not_2_out;

  not not_1 (not_1_out, 1'b1);
  not not_2 (not_2_out, 1'b1);
  MagnitudeComparator magnitudecomparator_1 (
    .A(A[7]), .B(B[7]), .Igt(not_1_out), .Ieq(1'b1), .Ilt(not_2_out), .AgtB(magnitudecomparator_1_agtb),
    .AeqB(magnitudecomparator_1_aeqb), .AltB(magnitudecomparator_1_altb));
  MagnitudeComparator magnitudecomparator_2 (
    .A(A[6]), .B(B[6]), .Igt(magnitudecomparator_1_agtb), .Ieq(magnitudecomparator_1_aeqb),
    .Ilt(magnitudecomparator_1_altb), .AgtB(magnitudecomparator_2_agtb), .AeqB(magnitudecomparator_2_aeqb),
    .AltB(magnitudecomparator_2_altb));
  MagnitudeComparator magnitudecomparator_3 (
    .A(A[5]), .B(B[5]), .Igt(magnitudecomparator_2_agtb), .Ieq(magnitudecomparator_2_aeqb),
    .Ilt(magnitudecomparator_2_altb), .AgtB(magnitudecomparator_3_agtb), .AeqB(magnitudecomparator_3_aeqb),
    .AltB(magnitudecomparator_3_altb));
  MagnitudeComparator magnitudecomparator_4 (
    .A(A[4]), .B(B[4]), .Igt(magnitudecomparator_3_agtb), .Ieq(magnitudecomparator_3_aeqb),
    .Ilt(magnitudecomparator_3_altb), .AgtB(magnitudecomparator_4_agtb), .AeqB(magnitudecomparator_4_aeqb),
    .AltB(magnitudecomparator_4_altb));
  MagnitudeComparator magnitudecomparator_5 (
    .A(A[3]), .B(B[3]), .Igt(magnitudecomparator_4_agtb), .Ieq(magnitudecomparator_4_aeqb),
    .Ilt(magnitudecomparator_4_altb), .AgtB(magnitudecomparator_5_agtb), .AeqB(magnitudecomparator_5_aeqb),
    .AltB(magnitudecomparator_5_altb));
  MagnitudeComparator magnitudecomparator_6 (
    .A(A[2]), .B(B[2]), .Igt(magnitudecomparator_5_agtb), .Ieq(magnitudecomparator_5_aeqb),
    .Ilt(magnitudecomparator_5_altb), .AgtB(magnitudecomparator_6_agtb), .AeqB(magnitudecomparator_6_aeqb),
    .AltB(magnitudecomparator_6_altb));
  MagnitudeComparator magnitudecomparator_7 (
    .A(A[1]), .B(B[1]), .Igt(magnitudecomparator_6_agtb), .Ieq(magnitudecomparator_6_aeqb),
    .Ilt(magnitudecomparator_6_altb), .AgtB(magnitudecomparator_7_agtb), .AeqB(magnitudecomparator_7_aeqb),
    .AltB(magnitudecomparator_7_altb));
  MagnitudeComparator magnitudecomparator_8 (
    .A(A[0]), .B(B[0]), .Igt(magnitudecomparator_7_agtb), .Ieq(magnitudecomparator_7_aeqb),
    .Ilt(magnitudecomparator_7_altb), .AgtB(AgtB), .AeqB(AeqB), .AltB(AltB));
endmodule

module ShiftControl (
  input  [7:0] Data,
  input  x,
  input  y,
  input  z,
  output [7:0] shiftedData
);

  wire [7:0] shiftfour_1_shifteddata, shifttwo_1_shifteddata;

  ShiftFour shiftfour_1 (.data(Data), .x_e(x), .shiftedData(shiftfour_1_shifteddata));
  ShiftTwo shifttwo_1 (.data(shiftfour_1_shifteddata), .y_e(y), .shiftedData(shifttwo_1_shifteddata));
  ShiftOne shiftone_1 (.data(shifttwo_1_shifteddata), .z_e(z), .shiftedData(shiftedData));
endmodule

module ShiftFour (
  input  [7:0] data,
  input  x_e,
  output [7:0] shiftedData
);

  wire [7:0] shifttwo_1_shifteddata;

  ShiftTwo shifttwo_1 (.data(data), .y_e(x_e), .shiftedData(shifttwo_1_shifteddata));
  ShiftTwo shifttwo_2 (.data(shifttwo_1_shifteddata), .y_e(x_e), .shiftedData(shiftedData));
endmodule

module ShiftTwo (
  input  [7:0] data,
  input  y_e,
  output [7:0] shiftedData
);

  wire [7:0] shiftone_1_shifteddata;

  ShiftOne shiftone_1 (.data(data), .z_e(y_e), .shiftedData(shiftone_1_shifteddata));
  ShiftOne shiftone_2 (.data(shiftone_1_shifteddata), .z_e(y_e), .shiftedData(shiftedData));
endmodule

module ShiftOne (
  input  [7:0] data,
  input  z_e,
  output [7:0] shiftedData
);

  wire not_1_out;

  Multiplexer multiplexer_1 (.in0(data[7]), .in1(data[6]), .out(shiftedData[7]), .sel(z_e));
  Multiplexer multiplexer_2 (.in0(data[6]), .in1(data[5]), .out(shiftedData[6]), .sel(z_e));
  Multiplexer multiplexer_3 (.in0(data[5]), .in1(data[4]), .out(shiftedData[5]), .sel(z_e));
  Multiplexer multiplexer_4 (.in0(data[4]), .in1(data[3]), .out(shiftedData[4]), .sel(z_e));
  Multiplexer multiplexer_5 (.in0(data[3]), .in1(data[2]), .out(shiftedData[3]), .sel(z_e));
  Multiplexer multiplexer_6 (.in0(data[2]), .in1(data[1]), .out(shiftedData[2]), .sel(z_e));
  Multiplexer multiplexer_7 (.in0(data[1]), .in1(data[0]), .out(shiftedData[1]), .sel(z_e));
  not not_1 (not_1_out, 1'b1);
  Multiplexer multiplexer_8 (.in0(data[0]), .in1(not_1_out), .out(shiftedData[0]), .sel(z_e));
endmodule

module blinkerDecoder (
  input  enable
);

  wire and_1_out, and_3_out, and_4_out, clock_1_out, decoder_1_out0, decoder_1_out1, decoder_1_out2,
       decoder_1_out3, decoder_1_out4, decoder_1_out5, decoder_1_out6, decoder_1_out7, decoder_1_out8,
       decoder_1_out9, decoder_1_out10, decoder_1_out11, decoder_1_out12, decoder_1_out13, decoder_1_out14,
       decoder_1_out15, decoder_1_out16, decoder_1_out17, decoder_1_out18, decoder_1_out19, decoder_1_out20,
       decoder_1_out21, decoder_1_out22, decoder_1_out23, decoder_1_out24, not_4_out, not_5_out, not_6_out,
       not_7_out, not_8_out, not_9_out, not_10_out;
  wire [4:0] counter_1_q, not_1_out;

  Clock clock_1 (.out(clock_1_out));
  not not_1 (not_1_out[0], not_1_out[4]);
  not not_2 (not_1_out[1], not_1_out[4]);
  not not_3 (not_1_out[2], not_1_out[4]);
  LED led_1 (.in(decoder_1_out0));
  Counter #(.max('h1f), .width(5)) counter_1 (
    .clr(and_1_out), .load(not_1_out[4]), .up(not_4_out), .clk(clock_1_out),
    .D({{2{not_1_out[4]}}, not_1_out[2:0]}), .Q(counter_1_q));  // open: count, carry
  not not_4 (not_4_out, enable);
  and and_1 (and_1_out, not_5_out, and_3_out);
  and and_2 (not_1_out[4], enable, and_4_out);
  LED led_2 (.in(decoder_1_out1));
  LED led_3 (.in(decoder_1_out2));
  not not_5 (not_5_out, enable);
  LED led_4 (.in(decoder_1_out3));
  LED led_5 (.in(decoder_1_out4));
  LED led_6 (.in(decoder_1_out5));
  LED led_7 (.in(decoder_1_out6));
  LED led_8 (.in(decoder_1_out7));
  LED led_9 (.in(decoder_1_out8));
  Decoder #(.select(5)) decoder_1 (
    .out0(decoder_1_out0), .out1(decoder_1_out1), .out2(decoder_1_out2), .out3(decoder_1_out3),
    .out4(decoder_1_out4), .out5(decoder_1_out5), .out6(decoder_1_out6), .out7(decoder_1_out7),
    .out8(decoder_1_out8), .out9(decoder_1_out9), .out10(decoder_1_out10), .out11(decoder_1_out11),
    .out12(decoder_1_out12), .out13(decoder_1_out13), .out14(decoder_1_out14), .out15(decoder_1_out15),
    .out16(decoder_1_out16), .out17(decoder_1_out17), .out18(decoder_1_out18), .out19(decoder_1_out19),
    .out20(decoder_1_out20), .out21(decoder_1_out21), .out22(decoder_1_out22), .out23(decoder_1_out23),
    .out24(decoder_1_out24), .sel(counter_1_q));  // open: out25, out26, out27, out28, out29, out30, out31, en
  not not_6 (not_6_out, counter_1_q[1]);
  not not_7 (not_7_out, counter_1_q[2]);
  not not_8 (not_8_out, counter_1_q[0]);
  not not_9 (not_9_out, counter_1_q[3]);
  not not_10 (not_10_out, counter_1_q[4]);
  LED led_10 (.in(decoder_1_out9));
  LED led_11 (.in(decoder_1_out10));
  and and_3 (and_3_out, counter_1_q[0], not_6_out, not_7_out, counter_1_q[3], counter_1_q[4]);
  and and_4 (and_4_out, not_8_out, not_6_out, not_7_out, not_9_out, not_10_out);
  LED led_12 (.in(decoder_1_out12));
  LED led_13 (.in(decoder_1_out11));
  LED led_14 (.in(decoder_1_out13));
  LED led_15 (.in(decoder_1_out14));
  LED led_16 (.in(decoder_1_out15));
  LED led_17 (.in(decoder_1_out16));
  LED led_18 (.in(decoder_1_out17));
  LED led_19 (.in(decoder_1_out18));
  LED led_20 (.in(decoder_1_out19));
  LED led_21 (.in(decoder_1_out20));
  LED led_22 (.in(decoder_1_out21));
  LED led_23 (.in(decoder_1_out22));
  LED led_24 (.in(decoder_1_out23));
  LED led_25 (.in(decoder_1_out24));
endmodule

module blinkerROM (
  input  enable
);

  wire and_1_out, and_3_out, and_4_out, clock_1_out, not_1_out, not_5_out, not_6_out, not_7_out, not_8_out,
       not_9_out, not_10_out;
  wire [4:0] counter_1_q, not_2_out;
  wire [24:0] rom_1_data;

  Clock clock_1 (.out(clock_1_out));
  not not_1 (not_1_out, enable);
  not not_2 (not_2_out[0], not_2_out[4]);
  not not_3 (not_2_out[1], not_2_out[4]);
  not not_4 (not_2_out[2], not_2_out[4]);
  Counter #(.max('h1f), .width(5)) counter_1 (
    .clr(and_1_out), .load(not_2_out[4]), .up(not_1_out), .clk(clock_1_out),
    .D({{2{not_2_out[4]}}, not_2_out[2:0]}), .Q(counter_1_q));  // open: count, carry
  not not_5 (not_5_out, enable);
  and and_1 (and_1_out, not_5_out, and_3_out);
  and and_2 (not_2_out[4], enable, and_4_out);
  not not_6 (not_6_out, counter_1_q[1]);
  not not_7 (not_7_out, counter_1_q[2]);
  not not_8 (not_8_out, counter_1_q[0]);
  not not_9 (not_9_out, counter_1_q[3]);
  not not_10 (not_10_out, counter_1_q[4]);
  LED led_1 (.in(rom_1_data[24]));
  LED led_2 (.in(rom_1_data[23]));
  ROM #(.addrWidth(5), .dataWidth(25)) rom_1 (.addr(counter_1_q), .data(rom_1_data));
  and and_3 (and_3_out, counter_1_q[0], not_6_out, not_7_out, counter_1_q[3], counter_1_q[4]);
  and and_4 (and_4_out, not_8_out, not_6_out, not_7_out, not_9_out, not_10_out);
  LED led_3 (.in(rom_1_data[22]));
  LED led_4 (.in(rom_1_data[21]));
  LED led_5 (.in(rom_1_data[20]));
  LED led_6 (.in(rom_1_data[19]));
  LED led_7 (.in(rom_1_data[17]));
  LED led_8 (.in(rom_1_data[18]));
  LED led_9 (.in(rom_1_data[16]));
  LED led_10 (.in(rom_1_data[15]));
  LED led_11 (.in(rom_1_data[14]));
  LED led_12 (.in(rom_1_data[13]));
  LED led_13 (.in(rom_1_data[12]));
  LED led_14 (.in(rom_1_data[11]));
  LED led_15 (.in(rom_1_data[10]));
  LED led_16 (.in(rom_1_data[9]));
  LED led_17 (.in(rom_1_data[8]));
  LED led_18 (.in(rom_1_data[7]));
  LED led_19 (.in(rom_1_data[6]));
  LED led_20 (.in(rom_1_data[5]));
  LED led_21 (.in(rom_1_data[4]));
  LED led_22 (.in(rom_1_data[3]));
  LED led_23 (.in(rom_1_data[2]));
  LED led_24 (.in(rom_1_data[1]));
  LED led_25 (.in(rom_1_data[0]));

  // Notes on the sheet:
  //   contents of rom_1 (hex, n*v repeats v):
  //   1 2 4 8 10 20 40 80 100 200 400 800 1000 2000 4000 8000 10000 20000 40000 80000 100000 200000 400000
  //   800000 1000000
endmodule

module main (
  input  enable,
  input  [7:0] address,
  input  [7:0] control_signal,
  input  [7:0] Data_w,
  input  [7:0] Input1,
  input  [7:0] Input2,
  input  [7:0] Input3,
  input  [7:0] Input4,
  output [7:0] Data_r,
  output [7:0] Output1,
  output [7:0] Output2,
  output [7:0] Output3,
  output [7:0] Output4
);

  wire and_1_out, clock_1_out, decoder_1_out1, decoder_1_out2, decoder_1_out3, decoder_1_out4,
       decoder_1_out5, or_1_out;
  wire [7:0] controlled_buffer_1_out, controlled_buffer_2_out, controlled_buffer_4_out,
       controlled_buffer_5_out, io_unit_1_databusout, ram_1_dout, rom_1_data;

  Clock clock_1 (.out(clock_1_out));
  and and_1 (and_1_out, clock_1_out, enable);
  Decoder #(.select(3)) decoder_1 (
    .out1(decoder_1_out1), .out2(decoder_1_out2), .out3(decoder_1_out3), .out4(decoder_1_out4),
    .out5(decoder_1_out5), .sel(control_signal[2:0]));  // open: out0, out6, out7, en
  assign controlled_buffer_1_out = decoder_1_out5 ? Data_w : 8'bz;  // Controlled_Buffer controlled_buffer_1
  assign controlled_buffer_2_out = decoder_1_out1 ? address : 8'bz;  // Controlled_Buffer controlled_buffer_2
  ROM rom_1 (.addr(controlled_buffer_2_out), .data(rom_1_data));
  IO_unit io_unit_1 (
    .clk(and_1_out), .DataBusIn(controlled_buffer_1_out), .input00000001(Input1), .input00000010(Input2),
    .input00000011(Input3), .input00000100(Input4), .controlBus(control_signal), .AddrBus(address),
    .output00000101(Output1), .output00000110(Output2), .output00000111(Output3), .output00001000(Output4),
    .DataBusOut(io_unit_1_databusout));
  assign Data_r = decoder_1_out1 ? rom_1_data : 8'bz;  // Controlled_Buffer controlled_buffer_3
  assign controlled_buffer_4_out = or_1_out ? address : 8'bz;  // Controlled_Buffer controlled_buffer_4
  RAM ram_1 (
    .addr(controlled_buffer_4_out), .we(decoder_1_out3), .oe(decoder_1_out2), .clk(and_1_out),
    .din(controlled_buffer_5_out), .dout(ram_1_dout));
  assign controlled_buffer_5_out = decoder_1_out3 ? Data_w : 8'bz;  // Controlled_Buffer controlled_buffer_5
  or or_1 (or_1_out, decoder_1_out2, decoder_1_out3);
  assign Data_r = decoder_1_out4 ? io_unit_1_databusout : 8'bz;  // Controlled_Buffer controlled_buffer_6
  assign Data_r = decoder_1_out2 ? ram_1_dout : 8'bz;  // Controlled_Buffer controlled_buffer_7

  // Notes on the sheet:
  //   contents of rom_1 (hex, n*v repeats v):
  //   11
endmodule

module IO_unit (
  input  clk,
  input  [7:0] DataBusIn,
  input  [7:0] input00000001,
  input  [7:0] input00000010,
  input  [7:0] input00000011,
  input  [7:0] input00000100,
  input  [7:0] controlBus,
  input  [7:0] AddrBus,
  output [7:0] output00000101,
  output [7:0] output00000110,
  output [7:0] output00000111,
  output [7:0] output00001000,
  output [7:0] DataBusOut
);

  wire eight_out, five_out, four_out, not_1_out, not_2_out, not_3_out, not_4_out, not_5_out, not_6_out,
       not_7_out, not_8_out, not_9_out, not_10_out, not_11_out, not_12_out, not_13_out, not_14_out,
       not_15_out, not_16_out, not_17_out, not_18_out, not_19_out, not_20_out, not_21_out, not_22_out,
       not_23_out, not_24_out, not_25_out, not_26_out, not_27_out, not_28_out, not_29_out, not_30_out,
       not_31_out, not_32_out, one_out, r0001_out, r0010_out, r0011_out, r0100_out, read_out, seven_out,
       six_out, three_out, two_out, w0101_out, w0110_out, w0111_out, w1000_out, write_out;
  wire [1:0] priority_encoder_1_out;

  Register First (.D(DataBusIn), .en(w0101_out), .clk(clk), .Q(output00000101));  // open: clr
  and r0001 (r0001_out, read_out, one_out);
  not not_1 (not_1_out, controlBus[0]);
  not not_2 (not_2_out, controlBus[1]);
  not not_3 (not_3_out, controlBus[3]);
  not not_4 (not_4_out, controlBus[4]);
  not not_5 (not_5_out, controlBus[5]);
  not not_6 (not_6_out, controlBus[6]);
  not not_7 (not_7_out, controlBus[7]);
  not not_8 (not_8_out, controlBus[1]);
  not not_9 (not_9_out, controlBus[3]);
  not not_10 (not_10_out, controlBus[4]);
  not not_11 (not_11_out, controlBus[5]);
  not not_12 (not_12_out, controlBus[6]);
  not not_13 (not_13_out, controlBus[7]);
  and r0010 (r0010_out, read_out, two_out);
  and read (read_out, not_1_out, not_2_out, controlBus[2], not_3_out, not_4_out, not_5_out, not_6_out, not_7_out);
  and write (write_out, controlBus[0], not_8_out, controlBus[2], not_9_out, not_10_out, not_11_out, not_12_out, not_13_out);
  not not_14 (not_14_out, AddrBus[1]);
  not not_15 (not_15_out, AddrBus[2]);
  not not_16 (not_16_out, AddrBus[3]);
  not not_17 (not_17_out, AddrBus[0]);
  not not_18 (not_18_out, AddrBus[2]);
  not not_19 (not_19_out, AddrBus[3]);
  not not_20 (not_20_out, AddrBus[2]);
  not not_21 (not_21_out, AddrBus[3]);
  not not_22 (not_22_out, AddrBus[0]);
  not not_23 (not_23_out, AddrBus[1]);
  not not_24 (not_24_out, AddrBus[3]);
  not not_25 (not_25_out, AddrBus[1]);
  not not_26 (not_26_out, AddrBus[3]);
  not not_27 (not_27_out, AddrBus[0]);
  not not_28 (not_28_out, AddrBus[3]);
  not not_29 (not_29_out, AddrBus[3]);
  not not_30 (not_30_out, AddrBus[0]);
  not not_31 (not_31_out, AddrBus[1]);
  not not_32 (not_32_out, AddrBus[2]);
  Register Second (.D(DataBusIn), .en(w0110_out), .clk(clk), .Q(output00000110));  // open: clr
  and r0011 (r0011_out, read_out, three_out);
  and one (one_out, AddrBus[0], not_14_out, not_15_out, not_16_out);
  and two (two_out, not_17_out, AddrBus[1], not_18_out, not_19_out);
  and three (three_out, AddrBus[0], AddrBus[1], not_20_out, not_21_out);
  and four (four_out, not_22_out, not_23_out, AddrBus[2], not_24_out);
  and five (five_out, AddrBus[0], not_25_out, AddrBus[2], not_26_out);
  and six (six_out, not_27_out, AddrBus[1], AddrBus[2], not_28_out);
  and seven (seven_out, AddrBus[0], AddrBus[1], AddrBus[2], not_29_out);
  and eight (eight_out, not_30_out, not_31_out, not_32_out, AddrBus[3]);
  Register Third (.D(DataBusIn), .en(w0111_out), .clk(clk), .Q(output00000111));  // open: clr
  and r0100 (r0100_out, read_out, four_out);
  and w0101 (w0101_out, write_out, five_out);
  and w0110 (w0110_out, write_out, six_out);
  Register Fourth (.D(DataBusIn), .en(w1000_out), .clk(clk), .Q(output00001000));  // open: clr
  and w0111 (w0111_out, write_out, seven_out);
  and w1000 (w1000_out, write_out, eight_out);
  Priority_Encoder #(.select(2)) priority_encoder_1 (
    .in0(r0001_out), .in1(r0010_out), .in2(r0011_out), .in3(r0100_out), .out(priority_encoder_1_out));  // open: gs, en_out, en_in
  Multiplexer #(.select(2), .width(8)) multiplexer_1 (
    .in0(input00000001), .in1(input00000010), .in2(input00000011), .in3(input00000100), .out(DataBusOut),
    .sel(priority_encoder_1_out));
endmodule
