// Logisim project microcontroller.circ as structural Verilog: 1 circuit, main circuit lmfao
module lmfao (
  input  [7:0] address,
  input  [7:0] control_signal,
  input  [7:0] Data_w
);

  wire clock_1_out, decoder_1_out1, decoder_1_out2, decoder_1_out3;
  wire [7:0] controlled_buffer_1_out, controlled_buffer_2_out, controlled_buffer_3_out,
       controlled_buffer_4_out, ram_1_dout, rom_1_data;

  Decoder #(.select(3)) decoder_1 (
    .out1(decoder_1_out1), .out2(decoder_1_out2), .out3(decoder_1_out3), .sel(control_signal[2:0]));  // open: out0, out4, out5, out6, out7, en
  assign controlled_buffer_1_out = decoder_1_out1 ? address : 8'bz;  // Controlled_Buffer controlled_buffer_1
  ROM rom_1 (.addr(controlled_buffer_1_out), .data(rom_1_data));
  assign controlled_buffer_2_out = decoder_1_out1 ? rom_1_data : 8'bz;  // Controlled_Buffer controlled_buffer_2
  Clock clock_1 (.out(clock_1_out));
  assign controlled_buffer_3_out = decoder_1_out2 ? address : 8'bz;  // Controlled_Buffer controlled_buffer_3
  RAM ram_1 (
    .addr(controlled_buffer_3_out), .we(decoder_1_out3), .oe(decoder_1_out2), .clk(clock_1_out),
    .din(controlled_buffer_4_out), .dout(ram_1_dout));
  assign controlled_buffer_4_out = decoder_1_out3 ? Data_w : 8'bz;  // Controlled_Buffer controlled_buffer_4
  assign controlled_buffer_2_out = decoder_1_out2 ? ram_1_dout : 8'bz;  // Controlled_Buffer controlled_buffer_5
endmodule
