// Logisim project cpu.circ as structural Verilog
module fetch (
  input  [63:0] PC,
  input  clk,
  output [3:0] icode,
  output [3:0] ifun,
  output [3:0] rA,
  output [3:0] rB,
  output [63:0] valC,
  output [63:0] valP
);

  wire instruction_memory_1_need_regids, instruction_memory_1_need_valc;
  wire [7:0] instruction_memory_1_byte_1;
  wire [63:0] adder_1_out, adder_2_out, bit_extender_1_out, bit_extender_2_out, multiplier_1_out;

  assign bit_extender_1_out = {{63{1'b0}}, instruction_memory_1_need_valc};  // Bit_Extender bit_extender_1
  Adder #(.width(64)) adder_1 (.a(PC), .b(64'h1), .out(adder_1_out));  // open: cin, cout
  instruction_memory instruction_memory_1 (
    .PC(PC), .clk(clk), .need_regids(instruction_memory_1_need_regids),
    .need_valC(instruction_memory_1_need_valc), .byte_0({icode, ifun}), .byte_1(instruction_memory_1_byte_1),
    .byte_2(valC[63:56]), .byte_3(valC[55:48]), .byte_4(valC[47:40]), .byte_5(valC[39:32]),
    .byte_6(valC[31:24]), .byte_7(valC[23:16]), .byte_8(valC[15:8]), .byte_9(valC[7:0]));
  Multiplier #(.width(64)) multiplier_1 (.a(bit_extender_1_out), .b(64'h8), .out(multiplier_1_out));  // open: cin, cout
  Adder #(.width(64)) adder_2 (.a(multiplier_1_out), .b(adder_1_out), .out(adder_2_out));  // open: cin, cout
  assign bit_extender_2_out = {{63{1'b0}}, instruction_memory_1_need_regids};  // Bit_Extender bit_extender_2
  Multiplexer #(.width(4)) multiplexer_1 (
    .in0(4'b1111), .in1(instruction_memory_1_byte_1[7:4]), .out(rA), .sel(instruction_memory_1_need_regids));
  Multiplexer #(.width(4)) multiplexer_2 (
    .in0(4'b1111), .in1(instruction_memory_1_byte_1[3:0]), .out(rB), .sel(instruction_memory_1_need_regids));
  Adder #(.width(64)) adder_3 (.a(bit_extender_2_out), .b(adder_2_out), .out(valP));  // open: cin, cout
endmodule

module instruction_memory (
  input  [63:0] PC,
  input  clk,
  output need_regids,
  output need_valC,
  output [7:0] byte_0,
  output [7:0] byte_1,
  output [7:0] byte_2,
  output [7:0] byte_3,
  output [7:0] byte_4,
  output [7:0] byte_5,
  output [7:0] byte_6,
  output [7:0] byte_7,
  output [7:0] byte_8,
  output [7:0] byte_9
);

  wire and_1_out, and_2_out, and_3_out, and_4_out, and_5_out, and_6_out, and_7_out, and_8_out, and_9_out,
       and_10_out, comparator_1_eq, comparator_2_eq, comparator_3_eq, comparator_4_eq, comparator_5_eq,
       comparator_6_eq, comparator_7_eq, comparator_8_eq, comparator_9_eq, comparator_10_eq,
       comparator_11_eq, comparator_12_eq, decoder_1_out0, decoder_1_out1, decoder_1_out2, decoder_1_out3,
       decoder_1_out4, decoder_1_out5, decoder_1_out6, decoder_1_out7, decoder_1_out8, decoder_1_out9;
  wire [3:0] adder_1_out, multiplexer_1_out, register_1_q, subtractor_1_out;
  wire [7:0] ram_1_dout;
  wire [11:0] adder_2_out, bit_extender_1_out;

  Register #(.width(4)) register_1 (.D(adder_1_out), .en(clk), .clk(clk), .Q(register_1_q));  // open: clr
  Adder #(.width(4)) adder_1 (.a(register_1_q), .b(4'b0001), .out(adder_1_out));  // open: cin, cout
  Subtractor #(.width(4)) subtractor_1 (.a(register_1_q), .b(4'b0001), .out(subtractor_1_out));  // open: bin, bout
  and and_1 (and_1_out, need_valC, ~need_regids);  // AND_Gate
  assign bit_extender_1_out = {{8{1'b0}}, multiplexer_1_out};  // Bit_Extender bit_extender_1
  Multiplexer #(.width(4)) multiplexer_1 (
    .in0(register_1_q), .in1(subtractor_1_out), .out(multiplexer_1_out), .sel(and_1_out));
  RAM #(.addrWidth(12), .enables("line"), .\type ("nonvolatile")) ram_1 (
    .addr(adder_2_out), .clk(clk), .dout(ram_1_dout));  // open: we, din
  Adder #(.width(12)) adder_2 (.a(PC[11:0]), .b(bit_extender_1_out), .out(adder_2_out));  // open: cin, cout
  Comparator #(.width(4)) comparator_1 (.a(byte_0[7:4]), .b(4'b0010), .eq(comparator_1_eq));  // open: gt, lt
  Comparator #(.width(4)) comparator_2 (.a(byte_0[7:4]), .b(4'b0011), .eq(comparator_2_eq));  // open: gt, lt
  Comparator #(.width(4)) comparator_3 (.a(byte_0[7:4]), .b(4'b0100), .eq(comparator_3_eq));  // open: gt, lt
  Comparator #(.width(4)) comparator_4 (.a(byte_0[7:4]), .b(4'b0101), .eq(comparator_4_eq));  // open: gt, lt
  Comparator #(.width(4)) comparator_5 (.a(byte_0[7:4]), .b(4'b0110), .eq(comparator_5_eq));  // open: gt, lt
  Comparator #(.width(4)) comparator_6 (.a(byte_0[7:4]), .b(4'b1010), .eq(comparator_6_eq));  // open: gt, lt
  Comparator #(.width(4)) comparator_7 (.a(byte_0[7:4]), .b(4'b1011), .eq(comparator_7_eq));  // open: gt, lt
  Comparator #(.width(4)) comparator_8 (.a(byte_0[7:4]), .b(4'b0011), .eq(comparator_8_eq));  // open: gt, lt
  Comparator #(.width(4)) comparator_9 (.a(byte_0[7:4]), .b(4'b0100), .eq(comparator_9_eq));  // open: gt, lt
  Comparator #(.width(4)) comparator_10 (.a(byte_0[7:4]), .b(4'b0101), .eq(comparator_10_eq));  // open: gt, lt
  Comparator #(.width(4)) comparator_11 (.a(byte_0[7:4]), .b(4'b0111), .eq(comparator_11_eq));  // open: gt, lt
  Comparator #(.width(4)) comparator_12 (.a(byte_0[7:4]), .b(4'b1000), .eq(comparator_12_eq));  // open: gt, lt
  or or_1 (need_valC, comparator_8_eq, comparator_9_eq, comparator_10_eq, comparator_11_eq, comparator_12_eq);
  or or_2 (need_regids, comparator_1_eq, comparator_2_eq, comparator_3_eq, comparator_4_eq, comparator_5_eq, comparator_6_eq, comparator_7_eq);
  Decoder #(.enable("false"), .select(4)) decoder_1 (
    .out0(decoder_1_out0), .out1(decoder_1_out1), .out2(decoder_1_out2), .out3(decoder_1_out3),
    .out4(decoder_1_out4), .out5(decoder_1_out5), .out6(decoder_1_out6), .out7(decoder_1_out7),
    .out8(decoder_1_out8), .out9(decoder_1_out9), .sel(register_1_q));  // open: out10, out11, out12, out13, out14, out15
  Register register_2 (.D(ram_1_dout), .en(decoder_1_out0), .clk(clk), .Q(byte_0));  // open: clr
  Register register_3 (.D(ram_1_dout), .en(and_2_out), .clk(clk), .Q(byte_1));  // open: clr
  and and_2 (and_2_out, need_regids, decoder_1_out1);
  Register register_4 (.D(ram_1_dout), .en(and_3_out), .clk(clk), .Q(byte_2));  // open: clr
  and and_3 (and_3_out, need_valC, decoder_1_out2);
  Register register_5 (.D(ram_1_dout), .en(and_4_out), .clk(clk), .Q(byte_3));  // open: clr
  and and_4 (and_4_out, need_valC, decoder_1_out3);
  Register register_6 (.D(ram_1_dout), .en(and_5_out), .clk(clk), .Q(byte_4));  // open: clr
  and and_5 (and_5_out, need_valC, decoder_1_out4);
  Register register_7 (.D(ram_1_dout), .en(and_6_out), .clk(clk), .Q(byte_5));  // open: clr
  and and_6 (and_6_out, need_valC, decoder_1_out5);
  Register register_8 (.D(ram_1_dout), .en(and_7_out), .clk(clk), .Q(byte_6));  // open: clr
  and and_7 (and_7_out, need_valC, decoder_1_out6);
  Register register_9 (.D(ram_1_dout), .en(and_8_out), .clk(clk), .Q(byte_7));  // open: clr
  and and_8 (and_8_out, need_valC, decoder_1_out7);
  Register register_10 (.D(ram_1_dout), .en(and_9_out), .clk(clk), .Q(byte_8));  // open: clr
  and and_9 (and_9_out, need_valC, decoder_1_out8);
  Register register_11 (.D(ram_1_dout), .en(and_10_out), .clk(clk), .Q(byte_9));  // open: clr
  and and_10 (and_10_out, need_valC, decoder_1_out9);
endmodule
